// Logisim project arm-1.circ as structural Verilog: 10 circuits, main circuit main
module main (
  output [3:0] ALUFlags
);

  wire clock_1_out, control_unit_bfab31f7_1_cp, control_unit_bfab31f7_1_ea, control_unit_bfab31f7_1_la,
       control_unit_bfab31f7_1_lb, control_unit_bfab31f7_1_li, control_unit_bfab31f7_1_lo,
       control_unit_bfab31f7_1_pcplus, control_unit_bfab31f7_1_pcsel, control_unit_bfab31f7_1_ressel,
       instr_data_memory_e81c88ac_1_p3;
  wire [1:0] control_unit_bfab31f7_1_su;
  wire [3:0] ir_1_output, ir_1_output_2;
  wire [7:0] ac_1_output, adder_1_out, b_1_output, bit_extender_1_out, controlled_buffer_1_out,
       instr_data_memory_e81c88ac_1_p2, instr_data_memory_e81c88ac_1_p5, multiplexer_1_out,
       multiplexer_2_out, o_1_output, pc_1_out_4;

  Clock clock_1 (.out(clock_1_out));
  PC pc_1 (
    .PC_ba757959(controlled_buffer_1_out), .CLK(clock_1_out), .Cp(control_unit_bfab31f7_1_cp),
    .out_4(pc_1_out_4));
  assign controlled_buffer_1_out = control_unit_bfab31f7_1_pcplus ? adder_1_out : 8'bz;  // Controlled_Buffer controlled_buffer_1
  Adder adder_1 (.a(pc_1_out_4), .b(8'h1), .out(adder_1_out));  // open: cin, cout
  Multiplexer #(.width(8)) multiplexer_1 (
    .in0(pc_1_out_4), .in1(bit_extender_1_out), .out(multiplexer_1_out), .sel(control_unit_bfab31f7_1_pcsel));
  assign bit_extender_1_out = {{4{ir_1_output_2[3]}}, ir_1_output_2};  // Bit_Extender bit_extender_1
  // Instr_Data_Memory_e81c88ac instr_data_memory_e81c88ac_1: pin names not known; wires that end beside it: multiplexer_1_out, instr_data_memory_e81c88ac_1_p2, instr_data_memory_e81c88ac_1_p3, clock_1_out, instr_data_memory_e81c88ac_1_p5
  IR ir_1 (
    .Input(instr_data_memory_e81c88ac_1_p5), .LI(control_unit_bfab31f7_1_li), .CLK(clock_1_out),
    .Output({ir_1_output_2, ir_1_output}));
  B b_1 (
    .Input(instr_data_memory_e81c88ac_1_p5), .LB(control_unit_bfab31f7_1_lb), .CLK(clock_1_out),
    .Output(b_1_output));
  Multiplexer #(.width(8)) multiplexer_2 (
    .in0(instr_data_memory_e81c88ac_1_p2), .in1(instr_data_memory_e81c88ac_1_p5), .out(multiplexer_2_out),
    .sel(control_unit_bfab31f7_1_ressel));
  AC ac_1 (
    .Input(multiplexer_2_out), .LA(control_unit_bfab31f7_1_la), .EA(control_unit_bfab31f7_1_ea),
    .Output(ac_1_output), .CLK(clock_1_out));
  ALU alu_1 (
    .Su(control_unit_bfab31f7_1_su), .A(ac_1_output), .B(b_1_output), .ALUFlags(ALUFlags),
    .Result(instr_data_memory_e81c88ac_1_p2));
  O o_1 (
    .Input(instr_data_memory_e81c88ac_1_p2), .LO(control_unit_bfab31f7_1_lo), .CLK(clock_1_out),
    .Output(o_1_output));
  Control_Unit_bfab31f7 control_unit_bfab31f7_1 (
    .CLK(clock_1_out), .Op(ir_1_output), .PCplus(control_unit_bfab31f7_1_pcplus),
    .Cp(control_unit_bfab31f7_1_cp), .PCsel(control_unit_bfab31f7_1_pcsel),
    .WE(instr_data_memory_e81c88ac_1_p3), .LI(control_unit_bfab31f7_1_li), .LB(control_unit_bfab31f7_1_lb),
    .RESsel(control_unit_bfab31f7_1_ressel), .LA(control_unit_bfab31f7_1_la),
    .LO(control_unit_bfab31f7_1_lo), .EA(control_unit_bfab31f7_1_ea), .Su(control_unit_bfab31f7_1_su));  // open: in_3
  Hex_Digit_Display hex_digit_display_1 (.value(o_1_output[3:0]));  // open: dp
  Hex_Digit_Display hex_digit_display_2 (.value(o_1_output[7:4]));  // open: dp
endmodule

module PC (
  input  [7:0] PC_ba757959,
  input  CLK,
  input  Cp,
  output [7:0] out_4
);

  wire and_1_out;

  Register register_1 (.D(PC_ba757959), .en(1'b1), .Q(out_4), .clk(and_1_out));  // open: clr
  and and_1 (and_1_out, CLK, Cp);
endmodule

module IR (
  input  [7:0] Input,
  input  CLK,
  input  LI,
  output [7:0] Output
);

  Register register_1 (.D(Input), .en(LI), .Q(Output), .clk(CLK));  // open: clr
endmodule

// Instr \ Data Memory
module Instr_Data_Memory_e81c88ac (
  input  [4:0] A,
  input  [7:0] WD,
  input  CLK,
  input  Cp,
  input  WE,
  output [7:0] RD
);

  wire not_1_out;
  wire [7:0] ram_1_data, rom_1_data, undriven;

  not not_1 (not_1_out, WE);
  RAM #(.addrWidth(5)) ram_1 (.addr(A), .data(ram_1_data), .clk(CLK), .ld(not_1_out));  // open: sel, clr
  ROM rom_1 (.addr(undriven), .data(rom_1_data), .sel(not_1_out));
  Multiplexer #(.width(8)) multiplexer_1 (.in0(ram_1_data), .in1(rom_1_data), .out(RD), .sel(Cp));

  // Notes on the sheet:
  //   contents of rom_1 (hex, n*v repeats v):
  //   4 1 1 1
endmodule

module AC (
  input  [7:0] Input,
  input  LA,
  input  CLK,
  input  EA,
  output [7:0] Output
);

  wire and_1_out, register_1_q, register_2_q;

  Register #(.width(1)) register_1 (.D(EA), .en(1'b1), .Q(register_1_q), .clk(CLK));  // open: clr
  Register #(.width(1)) register_2 (.D(register_1_q), .en(1'b1), .Q(register_2_q), .clk(CLK));  // open: clr
  Register register_3 (.D(Input), .en(LA), .Q(Output), .clk(CLK), .clr(and_1_out));
  and and_1 (and_1_out, register_2_q, ~EA);  // AND_Gate
endmodule

module B (
  input  [7:0] Input,
  input  CLK,
  input  LB,
  output [7:0] Output
);

  Register register_1 (.D(Input), .en(LB), .Q(Output), .clk(CLK));  // open: clr
endmodule

module ALU (
  input  [1:0] Su,
  input  [7:0] A,
  input  [7:0] B,
  output [3:0] ALUFlags,
  output [7:0] Result
);

  wire adder_2_cout, not_2_out, xnor_1_out, xor_1_out;
  wire [7:0] adder_1_out, adder_2_out, and_1_out, multiplexer_1_out, not_1_out, not_3_out, or_1_out;

  Adder adder_1 (.a(A), .b(B), .out(adder_1_out), .cin(1'b0));  // open: cout
  assign not_1_out = ~B;  // NOT_Gate not_1, 8 bits wide
  Multiplexer #(.enable("true"), .width(8)) multiplexer_1 (
    .in0(B), .in1(not_1_out), .out(multiplexer_1_out), .sel(Su[0]), .en(1'b1));
  Adder adder_2 (.a(A), .b(multiplexer_1_out), .out(adder_2_out), .cin(Su[0]), .cout(adder_2_cout));
  assign and_1_out = A & B;  // AND_Gate and_1, 8 bits wide
  assign or_1_out = A | B;  // OR_Gate or_1, 8 bits wide
  xor xor_1 (xor_1_out, adder_1_out[7], A[7]);
  not not_2 (not_2_out, Su[1]);
  NotExactlyOne xnor_1 (.out(xnor_1_out), .in0(A[7]), .in1(B[7]), .in2(Su[0]));
  Multiplexer #(.enable("true"), .select(2), .width(8)) multiplexer_2 (
    .in0(adder_2_out), .in1(adder_2_out), .in2(and_1_out), .in3(or_1_out), .out({ALUFlags[3], Result[6:0]}),
    .sel(Su), .en(1'b1));
  assign not_3_out = ~{ALUFlags[3], Result[6:0]};  // NOT_Gate not_3, 8 bits wide
  and and_2 (ALUFlags[0], xor_1_out, xnor_1_out, not_2_out);
  and and_3 (ALUFlags[1], not_2_out, adder_2_cout);
  and and_4 (ALUFlags[2], not_3_out[0], not_3_out[1], not_3_out[2], not_3_out[3], not_3_out[4], not_3_out[5], not_3_out[6], not_3_out[7]);

  assign Result[7] = ALUFlags[3];
endmodule

module O (
  input  [7:0] Input,
  input  CLK,
  input  LO,
  output [7:0] Output
);

  Register register_1 (.D(Input), .en(LO), .Q(Output), .clk(CLK));  // open: clr
endmodule

// Contol Unit
module Control_Unit_bfab31f7 (
  input  CLK,
  input  [3:0] Op,
  input  in_3,
  output PCplus,
  output Cp,
  output PCsel,
  output WE,
  output LI,
  output LB,
  output RESsel,
  output LA,
  output LO,
  output EA,
  output [1:0] Su
);

  wire and_1_out, and_2_out, and_3_out, and_4_out, and_5_out, and_6_out, and_7_out, and_8_out, and_9_out,
       and_10_out, and_11_out, controlled_buffer_3_out, d_ff_3_q, d_ff_5_p2, d_ff_6_q, d_ff_8_p3,
       decoder_1_out0, decoder_1_out1, decoder_1_out2, decoder_1_out3, decoder_1_out8, decoder_1_out9,
       decoder_1_out10, decoder_1_out11, decoder_1_out12, decoder_1_out13, decoder_1_out14, decoder_1_out15,
       not_1_out, or_1_out, or_2_out, or_3_out, or_4_out, or_6_out, or_7_out, or_8_out, undriven, undriven_2,
       undriven_3, undriven_4, undriven_5, undriven_6, undriven_7;
  wire [1:0] controlled_buffer_5_out, multiplexer_1_out, multiplexer_2_out, multiplexer_3_out,
       multiplexer_4_out, or_5_out;

  D_Flip_Flop d_ff_1 (.preset(CLK), .reset(1'b1));  // open: D, clk, Q, Qn
  or or_1 (or_1_out, and_1_out, undriven_3);
  D_Flip_Flop d_ff_2 (.clk(undriven_7), .reset(1'b1));  // open: D, Q, Qn, preset
  D_Flip_Flop d_ff_3 (.clk(in_3), .D(d_ff_8_p3), .Q(d_ff_3_q));  // open: Qn, preset, reset
  D_Flip_Flop d_ff_4 (.clk(undriven_7), .preset(CLK), .reset(1'b1));  // open: D, Q, Qn
  and and_1 (and_1_out, undriven_5, ~and_2_out);  // AND_Gate
  and and_2 (and_2_out, ~Op[2], ~Op[3]);  // AND_Gate
  // D_Flip_Flop d_ff_5: pin names not known; wires that end beside it: d_ff_3_q, d_ff_5_p2, in_3
  D_Flip_Flop d_ff_6 (.clk(in_3), .D(d_ff_5_p2), .Q(d_ff_6_q));  // open: Qn, preset, reset
  D_Flip_Flop d_ff_7 (.clk(undriven_7), .preset(undriven), .reset(undriven));  // open: D, Q, Qn
  // D_Flip_Flop d_ff_8: pin names not known; wires that end beside it: in_3, d_ff_6_q, d_ff_8_p3
  Decoder #(.select(4)) decoder_1 (
    .out0(decoder_1_out0), .out1(decoder_1_out1), .out2(decoder_1_out2), .out3(decoder_1_out3),
    .out8(decoder_1_out8), .out9(decoder_1_out9), .out10(decoder_1_out10), .out11(decoder_1_out11),
    .out12(decoder_1_out12), .out13(decoder_1_out13), .out14(decoder_1_out14), .out15(decoder_1_out15),
    .sel(Op));  // open: out4, out5, out6, out7, en
  or or_2 (or_2_out, decoder_1_out8, decoder_1_out9, decoder_1_out10, decoder_1_out11);
  not not_1 (not_1_out, decoder_1_out15);
  and and_3 (and_3_out, decoder_1_out14, undriven_6);
  and and_4 (and_4_out, undriven_6, or_2_out);
  or or_3 (or_3_out, decoder_1_out3, decoder_1_out2, decoder_1_out1, decoder_1_out0);
  Multiplexer #(.width(2)) multiplexer_1 (.in0(2'b00), .in1(2'b00), .out(multiplexer_1_out), .sel(decoder_1_out0));
  Multiplexer #(.width(2)) multiplexer_2 (.in0(2'b00), .in1(2'b01), .out(multiplexer_2_out), .sel(decoder_1_out1));
  Multiplexer #(.width(2)) multiplexer_3 (.in0(2'b00), .in1(2'b10), .out(multiplexer_3_out), .sel(decoder_1_out2));
  Multiplexer #(.width(2)) multiplexer_4 (.in0(2'b00), .in1(2'b11), .out(multiplexer_4_out), .sel(decoder_1_out3));
  assign PCplus = not_1_out ? undriven_4 : 1'bz;  // Controlled_Buffer controlled_buffer_1
  assign Cp = not_1_out ? undriven_4 : 1'bz;  // Controlled_Buffer controlled_buffer_2
  or or_4 (or_4_out, and_3_out, undriven_4);
  and and_5 (and_5_out, undriven_6, decoder_1_out12);
  and and_6 (and_6_out, undriven_6, or_3_out);
  assign or_5_out = multiplexer_1_out | multiplexer_2_out | multiplexer_3_out | multiplexer_4_out;  // OR_Gate or_5, 2 bits wide
  assign controlled_buffer_3_out = or_6_out ? or_4_out : 1'bz;  // Controlled_Buffer controlled_buffer_3
  or or_6 (or_6_out, undriven_2, undriven_4, and_7_out);
  and and_7 (and_7_out, decoder_1_out14, undriven_6);
  and and_8 (and_8_out, undriven_6, decoder_1_out13);
  assign LO = not_1_out ? and_4_out : 1'bz;  // Controlled_Buffer controlled_buffer_4
  assign controlled_buffer_5_out = and_6_out ? or_5_out : 2'bz;  // Controlled_Buffer controlled_buffer_5
  assign Su = not_1_out ? controlled_buffer_5_out : 2'bz;  // Controlled_Buffer controlled_buffer_6
  assign PCsel = not_1_out ? controlled_buffer_3_out : 1'bz;  // Controlled_Buffer controlled_buffer_7
  or or_7 (or_7_out, and_5_out, undriven);
  and and_9 (and_9_out, or_2_out, undriven_6);
  and and_10 (and_10_out, undriven_6, or_3_out);
  and and_11 (and_11_out, undriven_6, decoder_1_out14);
  assign WE = not_1_out ? and_3_out : 1'bz;  // Controlled_Buffer controlled_buffer_8
  assign LI = not_1_out ? undriven_2 : 1'bz;  // Controlled_Buffer controlled_buffer_9
  assign LB = not_1_out ? and_8_out : 1'bz;  // Controlled_Buffer controlled_buffer_10
  assign RESsel = not_1_out ? and_5_out : 1'bz;  // Controlled_Buffer controlled_buffer_11
  assign LA = not_1_out ? or_7_out : 1'bz;  // Controlled_Buffer controlled_buffer_12
  or or_8 (or_8_out, and_9_out, and_10_out, and_11_out);
  assign EA = not_1_out ? or_8_out : 1'bz;  // Controlled_Buffer controlled_buffer_13
endmodule

module \reg  (
  input  [7:0] WD,
  input  WE,
  input  [7:0] A,
  input  CLK,
  output [7:0] RD
);

  wire demultiplexer_1_out0, demultiplexer_1_out1, demultiplexer_1_out2, demultiplexer_1_out3, not_1_out;
  wire [7:0] register_1_q, register_2_q, register_3_q, register_4_q;

  Demultiplexer #(.enable("true"), .select(2)) demultiplexer_1 (
    .out0(demultiplexer_1_out0), .out1(demultiplexer_1_out1), .out2(demultiplexer_1_out2),
    .out3(demultiplexer_1_out3), .in(WE), .sel(A[1:0]), .en(1'b1));
  Register register_1 (.D(WD), .en(demultiplexer_1_out0), .Q(register_1_q), .clk(CLK));  // open: clr
  Register register_2 (.D(WD), .en(demultiplexer_1_out1), .Q(register_2_q), .clk(CLK));  // open: clr
  Register register_3 (.D(WD), .en(demultiplexer_1_out2), .Q(register_3_q), .clk(CLK));  // open: clr
  Register register_4 (.D(WD), .en(demultiplexer_1_out3), .Q(register_4_q), .clk(CLK));  // open: clr
  not not_1 (not_1_out, WE);
  Multiplexer #(.enable("true"), .select(2), .width(8)) multiplexer_1 (
    .in0(register_1_q), .in1(register_2_q), .in2(register_3_q), .in3(register_4_q), .out(RD), .sel(A[1:0]),
    .en(not_1_out));
endmodule
